// Logisim project lab8.circ as structural Verilog: 2 circuits, main circuit ParityGenerator
module XOR (
  input  X,
  input  Y,
  output out_3
);

  wire and_1_out, and_2_out, not_1_out, not_2_out;

  not not_1 (not_1_out, X);
  not not_2 (not_2_out, Y);
  and and_1 (and_1_out, Y, not_1_out);
  and and_2 (and_2_out, not_2_out, X);
  or or_1 (out_3, and_1_out, and_2_out);

  // Notes on the sheet:
  //   Use minterm expansion to create an XOR gate using AND + OR gates
endmodule

module ParityGenerator (
  input  X,
  input  Y,
  input  Z,
  output Parity
);

  wire and_1_out, and_2_out, and_3_out, and_4_out, not_1_out, not_2_out, not_3_out, not_4_out, or_1_out;

  not not_1 (not_1_out, X);
  not not_2 (not_2_out, Y);
  and and_1 (and_1_out, not_1_out, Y);
  and and_2 (and_2_out, X, not_2_out);
  not not_3 (not_3_out, Z);
  or or_1 (or_1_out, and_1_out, and_2_out);
  not not_4 (not_4_out, or_1_out);
  and and_3 (and_3_out, or_1_out, not_3_out);
  and and_4 (and_4_out, not_4_out, Z);
  or or_2 (Parity, and_3_out, and_4_out);

  // Notes on the sheet:
  //   Input Bits
  //   Julian Noeske
  //   Write your parity circuit here
  //   the output = 1 if an odd number of inputs (1 or 3) are 1, otherwise 0
  //   ONLY use: NOT, AND, OR, and any custom functions you write (included in the .circ submission)
  //   WRITE YOUR NAME AND PLEDGE SOMEWHERE IN THIS CIRCUIT
  //   I pledge my honor that I have abided by the Stevens Honor System
  //   Output Bit
endmodule
